# Fritzing sketch rom-flasher (saved by Fritzing 0.9.6b)
breadboards: 1

parts:
  Raspberry_Pi_B_rev1 = Raspberry Pi B rev1
  IC1 = MSGEQ7 [package=soic8]

nets:
  N1: Raspberry_Pi_B_rev1.3V3, IC1.DCOUT, IC1.RESET, IC1.CKIN
  N2: Raspberry_Pi_B_rev1.GND, IC1.STROBE
  N3: Raspberry_Pi_B_rev1.GPIO_10, IC1.AUDIO_IN
  N4: Raspberry_Pi_B_rev1.GPIO_9, IC1.GND
  N5: Raspberry_Pi_B_rev1.GPIO_11, IC1.CG
  N6: Raspberry_Pi_B_rev1.GPIO_8, IC1.VDD
